# Fritzing sketch Esquema Protoboard (saved by Fritzing 0.8.5b)
breadboards: 1

parts:
  WIZ820io1 = WIZ820io [part_number=WIZ820io]
  Componente1 = Arduino Nano (Rev3.0) (ICSP)
  U1 = LCD-16X2 [package=lcd-16x2]  # not connected
  Q1 = NPN-Transistor [package="TO92 [THT]"]
  Q2 = NPN-Transistor [package="TO92 [THT]"]
  Q3 = NPN-Transistor [part_number=BC337 package="TO92 [THT]"]
  Q4 = NPN-Transistor [package="TO92 [THT]"]
  R1 = Resistor [tolerance=±5% resistance=10k package=THT]
  R2 = Resistor [tolerance=±5% resistance=10k package=THT]
  R3 = Resistor [tolerance=±5% resistance=10k package=THT]
  R4 = Resistor [tolerance=±5% resistance=10k package=THT]
  R5 = Resistor [tolerance=±5% resistance=10k package=THT]
  R6 = Resistor [tolerance=±5% resistance=10k package=THT]

nets:
  GND: WIZ820io1.GND, Componente1.GND
  N1: WIZ820io1.MOSI, Componente1.D11/MOSI
  N2: WIZ820io1.SCLK, Componente1.D13/SCK
  N3: WIZ820io1.nSS, Componente1.D10
  N4: WIZ820io1.MISO, Componente1.D12/MISO
  N5: WIZ820io1.nRESET, Componente1.RESET
  VIN: WIZ820io1.VIN, Componente1.3V3
  N6: Componente1.5V, R5.Pin_0, R6.Pin_0
  N7: Componente1.A5, Q1.C, Q2.E, R4.Pin_1
  N8: Componente1.A4, Q3.C, Q4.E, R3.Pin_1
  N9: Q1.E, Q2.C, R6.Pin_1
  N10: Q1.B, Q2.B, R2.Pin_1
  N11: Q3.E, Q4.C, R5.Pin_1
  N12: Q3.B, Q4.B, R1.Pin_1
  N13: R1.Pin_0, R2.Pin_0, R3.Pin_0, R4.Pin_0
