# Fritzing sketch Esquema Protoboard2 (saved by Fritzing 0.8.5b)
breadboards: 2

parts:
  WIZ820io1 = WIZ820io [part_number=WIZ820io]
  Componente1 = Arduino Nano (Rev3.0) (ICSP)
  U1 = LCD-16X2 [package=lcd-16x2]  # not connected
  Q1 = NPN-Transistor [package="TO92 [THT]"]
  Q2 = NPN-Transistor [package="TO92 [THT]"]
  Q3 = NPN-Transistor [part_number=BC337 package="TO92 [THT]"]
  Q4 = NPN-Transistor [package="TO92 [THT]"]
  R1 = Resistor [tolerance=±5% resistance=10k package=THT]
  R2 = Resistor [tolerance=±5% resistance=10k package=THT]
  R3 = Resistor [tolerance=±5% resistance=10k package=THT]
  R4 = Resistor [tolerance=±5% resistance=10k package=THT]
  R5 = Resistor [tolerance=±5% resistance=10k package=THT]
  R6 = Resistor [tolerance=±5% resistance=10k package=THT]
  S1 = Pushbutton [package="[THT]"]
  S2 = Pushbutton [package="[THT]"]
  S3 = Pushbutton [package="[THT]"]
  S4 = Pushbutton [package="[THT]"]
  S5 = Pushbutton [package="[THT]"]
  R7 = Resistor [tolerance=±5% resistance=10k package=THT]
  R8 = Resistor [tolerance=±5% resistance=10k package=THT]
  R9 = Resistor [tolerance=±5% resistance=10k package=THT]
  R10 = Resistor [tolerance=±5% resistance=10k package=THT]
  R11 = Resistor [tolerance=±5% resistance=10k package=THT]

nets:
  GND: WIZ820io1.GND, Componente1.GND, R11.Pin_0
  N1: WIZ820io1.MOSI, Componente1.D11/MOSI
  N2: WIZ820io1.SCLK, Componente1.D13/SCK
  N3: WIZ820io1.nSS, Componente1.D10
  N4: WIZ820io1.MISO, Componente1.D12/MISO
  N5: WIZ820io1.nRESET, Componente1.RESET
  VIN: WIZ820io1.VIN, Componente1.3V3, S1.Pin_3, S1.Pin_4, S2.Pin_3, S2.Pin_4, S3.Pin_3, S3.Pin_4, S4.Pin_3, S4.Pin_4, S5.Pin_3, S5.Pin_4
  N6: Componente1.5V, R5.Pin_0, R6.Pin_0
  N7: Componente1.A5, Q1.C, Q2.E, R4.Pin_1
  N8: Componente1.A4, Q3.C, Q4.E, R3.Pin_1
  N9: Componente1.A0, S3.Pin_1, S3.Pin_2, R10.Pin_1, R11.Pin_1
  N10: Q1.E, Q2.C, R6.Pin_1
  N11: Q1.B, Q2.B, R2.Pin_1
  N12: Q3.E, Q4.C, R5.Pin_1
  N13: Q3.B, Q4.B, R1.Pin_1
  N14: R1.Pin_0, R2.Pin_0, R3.Pin_0, R4.Pin_0
  N15: S1.Pin_1, S1.Pin_2, R7.Pin_0
  N16: S2.Pin_1, S2.Pin_2, R7.Pin_1, R8.Pin_0
  N17: S4.Pin_1, S4.Pin_2, R8.Pin_1, R9.Pin_0
  N18: S5.Pin_1, S5.Pin_2, R9.Pin_1, R10.Pin_0
